# Fritzing sketch pixelMinion (saved by Fritzing 0.9.3b)
breadboards: 2

parts:
  JP1 = Header 4 [package=molex-1x4_lock]
  JP2 = Header 4 [package=molex-1x4_lock]
  LED1 = RGB LED (com. cathode, brg) [package="5 mm [THT]"]
  R1 = Resistor [tolerance=±5% resistance=470 package=THT]
  R2 = Resistor [tolerance=±5% resistance=470 package=THT]
  R3 = Resistor [tolerance=±5% resistance=1k package=THT]
  IC1 = Voltage Regulator [package=to-92]
  C1 = Capacitor [package=cap-pth-small2]
  Part2 = Arduino Nano (Rev3.0)

nets:
  GND: JP1.1, LED1.common_cathode, IC1.GND, C1.1, Part2.GND
  N1: JP1.2, Part2.D9
  N2: JP1.3, Part2.D13/SCK
  N3: JP1.4, Part2.D12/MISO
  N4: JP2.1, IC1.OUT, C1.2
  N5: JP2.2, Part2.D10
  N6: JP2.3, Part2.D11/MOSI
  N7: LED1.blue_anode, R3.Pin_0
  N8: LED1.red_anode, R2.Pin_0
  N9: LED1.green_anode, R1.Pin_0
  N10: R1.Pin_1, Part2.D3
  N11: R2.Pin_1, Part2.D5
  N12: R3.Pin_1, Part2.D6
  N13: IC1.IN, Part2.5V

notes:
  +5 V Input
  Output to
  Strip 0
  Output to
  Strip 1
  Flat side of LED
  faces this way.
  Black 3-pin device is S-812C33 3.3 V regulator. Flat side faces Nano.
  Capacitor is 10 µF MLCC, usually blue. Is non-polarized, so can be inserted either way.
  Connect A0 to GND for LED strip test (all pixels white).
  Connect A1 to GND for simulated measurements.

custom parts:
  RGB LED (com. cathode, brg): A 5mm tri-color LED with red, green and blue inside. Pin order: red - com. cathode - blue - green
  Voltage Regulator: Voltage Regulator S-812C Series
